# Fritzing sketch Basic_Soundboard_Attiny (saved by Fritzing 0.9.2b)
circuit board: 6.5cm x 2.5cm
breadboards: 1

parts:
  Voltage_Regulator = Voltage Regulator LM1117 [package=sot223]
  Swing = Resistor [tolerance=±5% resistance=0 package=THT]
  VCC1 = Battery
  C1 = Electrolytic Capacitor [capacitance=10µF package="100 mil [THT, electrolytic]"]
  BladeFet = TRANSISTOR_NPN [package=sot223]
  U2 = attiny85 [package=dip]
  Blade = female pin header, 2 pins [form="♀ (female)"]
  Button = female pin header, 2 pins [form="♀ (female)"]
  Clash = Tilt Switch [package=THT]
  J1 = female pin header, 8 pins [form="♀ (female)"]
  J2 = female pin header, 8 pins [form="♀ (female)"]
  SPKR = female pin header, 2 pins [form="♀ (female)"]

nets (from the pcb view):
  N1: Voltage_Regulator.ADJ, Swing.Pin_1, VCC1.-, C1.-, U2.Pin_4, Blade.pin2, Button.pin2, Clash.Pin_2, J2.pin8
  N2: Voltage_Regulator.OUT, C1.+, U2.Pin_8, J1.pin3
  N3: Voltage_Regulator.IN, VCC1.+, BladeFet.C
  N4: Swing.Pin_0, U2.Pin_2
  N5: BladeFet.B, U2.Pin_5
  N6: BladeFet.E, Blade.pin1
  N7: U2.Pin_3, Clash.Pin_1
  N8: U2.Pin_6, J1.pin7
  N9: U2.Pin_7, Button.pin1
  N10: J2.pin3, SPKR.pin1
  N11: J2.pin4, SPKR.pin2
